# Fritzing sketch ColorPicker (saved by Fritzing 0.8.3b)
circuit board: 5.13641cm x 3.97933cm
breadboards: 1

parts:
  Part1 = Arduino Micro (Rev3)
  LED1 = RGB LED (com. cathode, rbg) [package="5 mm [THT]"]
  R1 = Resistor [tolerance=±5% resistance=220 package=THT]
  R2 = Resistor [tolerance=±5% resistance=220 package=THT]
  R3 = Resistor [tolerance=±5% resistance=220 package=THT]
  LED2 = RGB LED (com. anode, rbg) [package="5 mm [THT]"]
  R7 = Resistor [tolerance=±5% resistance=220 package=THT]
  R8 = Resistor [tolerance=±5% resistance=220 package=THT]
  R9 = Resistor [tolerance=±5% resistance=220 package=THT]

nets:
  N1: Part1.5V, LED2.common_anode
  N2: Part1.GND, LED1.common_cathode
  N3: Part1.A5, R1.Pin_0
  N4: Part1.A4, R2.Pin_0
  N5: Part1.A3, R3.Pin_0
  N6: Part1.A2, R7.Pin_0
  N7: Part1.A1, R8.Pin_0
  N8: Part1.A0, R9.Pin_0
  N9: LED1.red_anode, R1.Pin_1
  N10: LED1.blue_anode, R2.Pin_1
  N11: LED1.green_anode, R3.Pin_1
  N12: LED2.red_cathode, R7.Pin_1
  N13: LED2.blue_cathode, R8.Pin_1
  N14: LED2.green_cathode, R9.Pin_1

notes:
  common chatode
  common anode
